// Logisim project 4bit_cpu_main.circ as structural Verilog: 12 circuits, main circuit main
module main (
  input  [31:0] ROM_IN,
  input  NEXT_CELL,
  input  START_ROM,
  input  [3:0] SET_0000,
  input  PC_READ,
  input  PC_WRITE,
  input  [3:0] END_MAKRO,
  input  [3:0] SET_0,
  input  PROGRAM,
  input  [3:0] COUNTER_SET_0001,
  input  PROG_READ,
  input  PROG_WRITE,
  output [3:0] CURRENT_INSTRUCTION,
  output [3:0] PROG_COUNTER,
  output [3:0] out_15,
  output [3:0] out_16,
  output [3:0] out_17,
  output [3:0] out_18,
  output [3:0] out_19,
  output [3:0] out_20
);

  wire A, A_R, ALU, B, B_R, bcd_to_7_segment_decoder_2_p1, binary_to_bcd_converter_1_p2, C, C_R, CLK, CRY, D,
       D_R, DATA, EN, F1, F2, RAM, READ, WRITE;
  wire [1:0] STATE;
  wire [3:0] ADR, alu_4bit_1_out_7, alu_4bit_1_z_flag, BUTTONS_sw4, controlled_buffer_1_out, DATA_1,
       IO_out_reg_13, IO_out_reg_14, RAM_ram_out, REG_A_data_out, REG_B_data_out;
  wire [7:0] rom_memory_1_rom_out;

  Clock u_C (.out(CLK));
  ROM_MEMORY rom_memory_1 (
    .ROM_IN_PROGRAM(ROM_IN), .NEXT_CELL(NEXT_CELL), .C(CLK), .START_PROGRAM(START_ROM), .SET_0000(SET_0000),
    .PC_READ(PC_READ), .PC_WRITE(PC_WRITE), .END_PROGRAM(END_MAKRO), .SET_0(SET_0), .FLAGS(out_20),
    .PROGRAM(PROGRAM), .COUNTER_SET_0001(COUNTER_SET_0001), .PROG_READ(PROG_READ), .PROG_WRITE(PROG_WRITE),
    .ROM_OUT({DATA_1, D, C, B, A, D_R, C_R, B_R, A_R, F2, F1, CRY, STATE, ADR, EN, WRITE, READ, rom_memory_1_rom_out}),
    .INSTRUCTION(CURRENT_INSTRUCTION), .PROG_COUNTER(PROG_COUNTER));
  DipSwitch #(.number(4)) BUTTONS (
    .sw1(BUTTONS_sw4[3]), .sw2(BUTTONS_sw4[2]), .sw3(BUTTONS_sw4[1]), .sw4(BUTTONS_sw4[0]));
  assign controlled_buffer_1_out = DATA ? DATA_1 : 4'bz;  // Controlled_Buffer controlled_buffer_1
  Decoder #(.select(2)) decoder_1 (.out0(DATA), .out1(ALU), .out2(RAM), .sel(STATE));  // open: out3, en
  assign controlled_buffer_1_out = RAM ? RAM_ram_out : 4'bz;  // Controlled_Buffer controlled_buffer_2
  RAM_MEMORY u_RAM (
    .RAM_IN(controlled_buffer_1_out), .REG_READ(READ), .REG_WRITE(WRITE), .ENABLE(EN), .ADDRES(ADR), .C(CLK),
    .RAM_OUT(RAM_ram_out));
  IO_MODULE IO (
    .I0_IN(controlled_buffer_1_out), .REG_READ(READ), .REG_WRITE(WRITE), .ENABLE(EN), .ADDRES(ADR),
    .PORT0_IN(BUTTONS_sw4), .C(CLK), .IO_OUT(RAM_ram_out), .OUT_REG_13(IO_out_reg_13),
    .OUT_REG_14(IO_out_reg_14));
  _7_Segment_Display u_7_segment_display_1 ();  // open: g, f, a, b, e, d, c, dp
  // BCD_to_7_Segment_decoder bcd_to_7_segment_decoder_1: pin names not known
  LedBar #(.matrixcols(4)) LED_1 (
    .led0(IO_out_reg_13[3]), .led1(IO_out_reg_13[2]), .led2(IO_out_reg_13[1]), .led3(IO_out_reg_13[0]));
  _7_Segment_Display u_7_segment_display_2 ();  // open: g, f, a, b, e, d, c, dp
  // BCD_to_7_Segment_decoder bcd_to_7_segment_decoder_2: pin names not known; wires that end beside it: bcd_to_7_segment_decoder_2_p1
  // Binary_to_BCD_converter #(.binvalue(4)) binary_to_bcd_converter_1: pin names not known; wires that end beside it: controlled_buffer_1_out, binary_to_bcd_converter_1_p2, binary_to_bcd_converter_1_p2, bcd_to_7_segment_decoder_2_p1
  LedBar #(.matrixcols(4)) LED_2 (
    .led0(IO_out_reg_14[3]), .led1(IO_out_reg_14[2]), .led2(IO_out_reg_14[1]), .led3(IO_out_reg_14[0]));
  REJESTR_4BIT REG_A (
    .DATA_IN(controlled_buffer_1_out), .REG_READ(A), .REG_WRITE(A_R), .C(CLK), .DATA_OUT(REG_A_data_out),
    .INSIDE_REG_DATA(out_15));
  REJESTR_4BIT REG_B (
    .DATA_IN(controlled_buffer_1_out), .REG_READ(B), .REG_WRITE(B_R), .C(CLK), .DATA_OUT(REG_B_data_out),
    .INSIDE_REG_DATA(out_18));
  LED led_1_dup2 (.in(alu_4bit_1_z_flag[0]));
  ALU_4BIT alu_4bit_1 (
    .DATA_1(REG_A_data_out), .DATA_2(REG_B_data_out), .CARRY_IN(CRY), .F1(F1), .F2(F2),
    .Z_FLAG(alu_4bit_1_z_flag[0]), .out_7(alu_4bit_1_out_7), .CARRY_OUT(alu_4bit_1_z_flag[1]));
  LED led_2_dup2 (.in(alu_4bit_1_z_flag[1]));
  assign controlled_buffer_1_out = ALU ? out_16 : 4'bz;  // Controlled_Buffer controlled_buffer_3
  Pull_Resistor pull_resistor_1 (.node(alu_4bit_1_z_flag[3]));
  REJESTR_4BIT REG_C (
    .DATA_IN(alu_4bit_1_out_7), .REG_READ(C), .REG_WRITE(C_R), .C(CLK), .DATA_OUT(out_16),
    .INSIDE_REG_DATA(out_17));
  REJESTR_4BIT REG_D (
    .DATA_IN({{2{alu_4bit_1_z_flag[3]}}, alu_4bit_1_z_flag[1:0]}), .REG_READ(D), .REG_WRITE(D_R), .C(CLK),
    .DATA_OUT(out_16), .INSIDE_REG_DATA(out_20));

  assign out_19 = out_16;

  // Other names for the same wires on the sheet: FLAGS[3:0] = out_20

  // Notes on the sheet:
  //   F1 F2
  //    0 0 ADD
  //   1 0 OR
  //   0 1 AND
  //   1 1 XOR
endmodule

module Adder_1bit (
  input  in_1,
  input  in_2,
  input  in_3,
  input  in_4,
  input  A,
  input  B,
  input  Cin,
  input  add_on,
  output SUM,
  output out_10
);

  wire and_1_out, and_2_out, and_3_out, and_4_out, and_5_out, and_6_out, or_1_out, xor_1_out, xor_2_out,
       xor_3_out, xor_4_out;

  xor xor_1 (xor_1_out, in_1, in_2);
  and and_1 (and_1_out, in_1, in_4, in_2);
  xor xor_2 (xor_2_out, A, B);
  and and_2 (and_2_out, A, B);
  and and_3 (and_3_out, xor_2_out, Cin);
  xor xor_3 (xor_3_out, xor_1_out, in_3);
  and and_4 (and_4_out, xor_1_out, in_4, in_3);
  xor xor_4 (xor_4_out, xor_2_out, Cin);
  or or_1 (or_1_out, and_3_out, and_2_out);
  or or_2 (out_10, and_1_out, and_4_out);
  and and_5 (and_5_out, xor_4_out, add_on);
  and and_6 (and_6_out, or_1_out, add_on);
  and and_7 (SUM, xor_3_out, in_4);
  LED S (.in(and_5_out));
  LED Cout (.in(and_6_out));

  // Notes on the sheet:
  //   Cin
  //   0
  //   0
  //   0
  //   0
  //   1
  //   1
  //   1
  //   1
  //   A
  //   B
  //   0   0
  //   0   1
  //   1   0
  //   1   1
  //   0
  //   0
  //   1
  //   0
  //   0
  //   1
  //   1
  //   1
  //   S
  //   Cout
  //   0
  //   0
  //   1
  //   0
  //   0
  //   1
  //   0
  //   1
  //   1
  //   0
  //   1
  //   0
  //   0
  //   1
  //   1
  //   1
endmodule

module MUX (
  input  A_MUX,
  input  B_MUX,
  output MUX_A,
  output MUX_B,
  output MUX_C,
  output MUX_D
);

  wire not_1_out, not_2_out, not_3_out, not_4_out;

  not not_1 (not_1_out, A_MUX);
  not not_2 (not_2_out, A_MUX);
  not not_3 (not_3_out, B_MUX);
  not not_4 (not_4_out, B_MUX);
  and and_1 (MUX_A, not_1_out, not_3_out);
  and and_2 (MUX_B, not_2_out, B_MUX);
  and and_3 (MUX_C, A_MUX, not_4_out);
  and and_4 (MUX_D, A_MUX, B_MUX);
endmodule

module LOGIC (
  input  AND_ON,
  input  A,
  input  B,
  input  OR_ON,
  input  COMPARE_ON,
  output LOGIC_AND,
  output LOGIC_OR,
  output COMPARE
);

  wire and_1_out, or_1_out, xor_1_out;

  and and_1 (and_1_out, A, B);
  or or_1 (or_1_out, A, B);
  xor xor_1 (xor_1_out, A, B);
  and and_2 (LOGIC_AND, and_1_out, AND_ON);
  and and_3 (LOGIC_OR, or_1_out, OR_ON);
  and and_4 (COMPARE, xor_1_out, COMPARE_ON);
endmodule

module ALU_1BIT (
  input  A,
  input  B,
  input  CIN,
  input  F1,
  input  F2,
  output ALU1BIT_OUT,
  output ALU1BIT_COUT
);

  wire adder_1bit_1_sum, logic_1_compare, logic_1_logic_and, logic_1_logic_or, mux_1_mux_a, mux_1_mux_b,
       mux_1_mux_c, mux_1_mux_d;

  MUX mux_1 (
    .A_MUX(F1), .B_MUX(F2), .MUX_A(mux_1_mux_a), .MUX_B(mux_1_mux_b), .MUX_C(mux_1_mux_c), .MUX_D(mux_1_mux_d));
  Adder_1bit adder_1bit_1 (
    .in_1(A), .in_2(B), .in_3(CIN), .in_4(mux_1_mux_a), .SUM(adder_1bit_1_sum), .out_10(ALU1BIT_COUT));  // open: A, B, Cin, add_on
  LOGIC logic_1 (
    .AND_ON(mux_1_mux_b), .A(A), .B(B), .OR_ON(mux_1_mux_c), .COMPARE_ON(mux_1_mux_d),
    .LOGIC_AND(logic_1_logic_and), .LOGIC_OR(logic_1_logic_or), .COMPARE(logic_1_compare));
  or or_1 (ALU1BIT_OUT, logic_1_logic_and, adder_1bit_1_sum, logic_1_logic_or, logic_1_compare);

  // Notes on the sheet:
  //   F1 F2
  //    0 0 ADD
  //   1 0 OR
  //   0 1 AND
  //   1 1 COMPARE
endmodule

module ALU_4BIT (
  input  [3:0] DATA_1,
  input  [3:0] DATA_2,
  input  CARRY_IN,
  input  F1,
  input  F2,
  output Z_FLAG,
  output [3:0] out_7,
  output CARRY_OUT
);

  wire alu_1bit_1_alu1bit_cout, alu_1bit_2_alu1bit_cout, alu_1bit_3_alu1bit_cout, not_1_out, not_2_out,
       not_3_out, not_4_out;

  ALU_1BIT alu_1bit_1 (
    .A(DATA_1[0]), .B(DATA_2[0]), .CIN(CARRY_IN), .F1(F1), .F2(F2), .ALU1BIT_OUT(out_7[0]),
    .ALU1BIT_COUT(alu_1bit_1_alu1bit_cout));
  ALU_1BIT alu_1bit_2 (
    .A(DATA_1[1]), .B(DATA_2[1]), .CIN(alu_1bit_1_alu1bit_cout), .F1(F1), .F2(F2), .ALU1BIT_OUT(out_7[1]),
    .ALU1BIT_COUT(alu_1bit_2_alu1bit_cout));
  ALU_1BIT alu_1bit_3 (
    .A(DATA_1[2]), .B(DATA_2[2]), .CIN(alu_1bit_2_alu1bit_cout), .F1(F1), .F2(F2), .ALU1BIT_OUT(out_7[2]),
    .ALU1BIT_COUT(alu_1bit_3_alu1bit_cout));
  ALU_1BIT alu_1bit_4 (
    .A(DATA_1[3]), .B(DATA_2[3]), .CIN(alu_1bit_3_alu1bit_cout), .F1(F1), .F2(F2), .ALU1BIT_OUT(out_7[3]),
    .ALU1BIT_COUT(CARRY_OUT));
  not not_1 (not_1_out, out_7[0]);
  not not_2 (not_2_out, out_7[1]);
  not not_3 (not_3_out, out_7[2]);
  not not_4 (not_4_out, out_7[3]);
  and and_1 (Z_FLAG, not_1_out, not_2_out, not_3_out, not_4_out);
endmodule

module REJESTR_4BIT (
  input  [3:0] DATA_IN,
  input  REG_READ,
  input  REG_WRITE,
  input  C,
  output [3:0] DATA_OUT,
  output [3:0] INSIDE_REG_DATA
);

  wire binary_to_bcd_converter_1_p2, binary_to_bcd_converter_1_p4;

  Register #(.width(4)) REG_A (.D(DATA_IN), .en(REG_WRITE), .clk(C), .Q(INSIDE_REG_DATA));  // open: clr
  assign DATA_OUT = REG_READ ? INSIDE_REG_DATA : 4'bz;  // Controlled_Buffer controlled_buffer_1
  _7_Segment_Display u_7_segment_display_1 ();  // open: g, f, a, b, e, d, c, dp
  // BCD_to_7_Segment_decoder bcd_to_7_segment_decoder_1: pin names not known
  // Binary_to_BCD_converter #(.binvalue(4)) binary_to_bcd_converter_1: pin names not known; wires that end beside it: INSIDE_REG_DATA, binary_to_bcd_converter_1_p2, binary_to_bcd_converter_1_p2, binary_to_bcd_converter_1_p4
  _7_Segment_Display u_7_segment_display_2 ();  // open: g, f, a, b, e, d, c, dp
  // BCD_to_7_Segment_decoder bcd_to_7_segment_decoder_2: pin names not known; wires that end beside it: binary_to_bcd_converter_1_p4
endmodule

module RAM_MEMORY (
  input  [3:0] RAM_IN,
  input  REG_READ,
  input  REG_WRITE,
  input  ENABLE,
  input  [3:0] ADDRES,
  input  C,
  output [3:0] RAM_OUT
);

  wire and_1_out, and_2_out, and_3_out, and_4_out, and_5_out, and_6_out, and_7_out, and_8_out, and_9_out,
       and_10_out, and_11_out, and_12_out, and_13_out, and_14_out, and_15_out, and_16_out, and_17_out,
       and_18_out, and_19_out, and_20_out, and_21_out, and_22_out, and_23_out, and_24_out, REG_1, REG_2,
       REG_3, REG_4, REG_5, REG_6, REG_7, REG_8, REG_9, REG_10, REG_11, REG_12;
  wire [3:0] REG_A_inside_reg_data, rejestr_4bit_1_inside_reg_data, rejestr_4bit_2_inside_reg_data,
       rejestr_4bit_3_inside_reg_data, rejestr_4bit_4_inside_reg_data, rejestr_4bit_5_inside_reg_data,
       rejestr_4bit_6_inside_reg_data, rejestr_4bit_7_inside_reg_data, rejestr_4bit_8_inside_reg_data,
       rejestr_4bit_9_inside_reg_data, rejestr_4bit_10_inside_reg_data, rejestr_4bit_11_inside_reg_data;

  Decoder #(.select(4)) decoder_1 (
    .out0(REG_1), .out1(REG_2), .out2(REG_3), .out3(REG_4), .out4(REG_5), .out5(REG_6), .out6(REG_7),
    .out7(REG_8), .out8(REG_9), .out9(REG_10), .out10(REG_11), .out11(REG_12), .sel(ADDRES), .en(ENABLE));  // open: out12, out13, out14, out15
  and and_1 (and_1_out, REG_READ, REG_1);
  and and_2 (and_2_out, REG_WRITE, REG_1);
  and and_3 (and_3_out, REG_READ, REG_2);
  and and_4 (and_4_out, REG_WRITE, REG_2);
  and and_5 (and_5_out, REG_READ, REG_3);
  and and_6 (and_6_out, REG_WRITE, REG_3);
  and and_7 (and_7_out, REG_READ, REG_4);
  and and_8 (and_8_out, REG_WRITE, REG_4);
  and and_9 (and_9_out, REG_READ, REG_5);
  and and_10 (and_10_out, REG_WRITE, REG_5);
  and and_11 (and_11_out, REG_READ, REG_6);
  and and_12 (and_12_out, REG_WRITE, REG_6);
  and and_13 (and_13_out, REG_READ, REG_7);
  and and_14 (and_14_out, REG_WRITE, REG_7);
  and and_15 (and_15_out, REG_READ, REG_8);
  and and_16 (and_16_out, REG_WRITE, REG_8);
  REJESTR_4BIT REG_A (
    .DATA_IN(RAM_IN), .REG_READ(and_1_out), .REG_WRITE(and_2_out), .C(C), .DATA_OUT(RAM_OUT),
    .INSIDE_REG_DATA(REG_A_inside_reg_data));
  REJESTR_4BIT rejestr_4bit_1 (
    .DATA_IN(RAM_IN), .REG_READ(and_3_out), .REG_WRITE(and_4_out), .C(C), .DATA_OUT(RAM_OUT),
    .INSIDE_REG_DATA(rejestr_4bit_1_inside_reg_data));
  REJESTR_4BIT rejestr_4bit_2 (
    .DATA_IN(RAM_IN), .REG_READ(and_5_out), .REG_WRITE(and_6_out), .C(C), .DATA_OUT(RAM_OUT),
    .INSIDE_REG_DATA(rejestr_4bit_2_inside_reg_data));
  REJESTR_4BIT rejestr_4bit_3 (
    .DATA_IN(RAM_IN), .REG_READ(and_7_out), .REG_WRITE(and_8_out), .C(C), .DATA_OUT(RAM_OUT),
    .INSIDE_REG_DATA(rejestr_4bit_3_inside_reg_data));
  REJESTR_4BIT rejestr_4bit_4 (
    .DATA_IN(RAM_IN), .REG_READ(and_9_out), .REG_WRITE(and_10_out), .C(C), .DATA_OUT(RAM_OUT),
    .INSIDE_REG_DATA(rejestr_4bit_4_inside_reg_data));
  REJESTR_4BIT rejestr_4bit_5 (
    .DATA_IN(RAM_IN), .REG_READ(and_11_out), .REG_WRITE(and_12_out), .C(C), .DATA_OUT(RAM_OUT),
    .INSIDE_REG_DATA(rejestr_4bit_5_inside_reg_data));
  REJESTR_4BIT rejestr_4bit_6 (
    .DATA_IN(RAM_IN), .REG_READ(and_13_out), .REG_WRITE(and_14_out), .C(C), .DATA_OUT(RAM_OUT),
    .INSIDE_REG_DATA(rejestr_4bit_6_inside_reg_data));
  REJESTR_4BIT rejestr_4bit_7 (
    .DATA_IN(RAM_IN), .REG_READ(and_15_out), .REG_WRITE(and_16_out), .C(C), .DATA_OUT(RAM_OUT),
    .INSIDE_REG_DATA(rejestr_4bit_7_inside_reg_data));
  and and_17 (and_17_out, REG_READ, REG_9);
  and and_18 (and_18_out, REG_WRITE, REG_9);
  and and_19 (and_19_out, REG_READ, REG_10);
  and and_20 (and_20_out, REG_WRITE, REG_10);
  and and_21 (and_21_out, REG_READ, REG_11);
  and and_22 (and_22_out, REG_WRITE, REG_11);
  and and_23 (and_23_out, REG_READ, REG_12);
  and and_24 (and_24_out, REG_WRITE, REG_12);
  REJESTR_4BIT rejestr_4bit_8 (
    .DATA_IN(RAM_IN), .REG_READ(and_17_out), .REG_WRITE(and_18_out), .C(C), .DATA_OUT(RAM_OUT),
    .INSIDE_REG_DATA(rejestr_4bit_8_inside_reg_data));
  REJESTR_4BIT rejestr_4bit_9 (
    .DATA_IN(RAM_IN), .REG_READ(and_19_out), .REG_WRITE(and_20_out), .C(C), .DATA_OUT(RAM_OUT),
    .INSIDE_REG_DATA(rejestr_4bit_9_inside_reg_data));
  REJESTR_4BIT rejestr_4bit_10 (
    .DATA_IN(RAM_IN), .REG_READ(and_21_out), .REG_WRITE(and_22_out), .C(C), .DATA_OUT(RAM_OUT),
    .INSIDE_REG_DATA(rejestr_4bit_10_inside_reg_data));
  REJESTR_4BIT rejestr_4bit_11 (
    .DATA_IN(RAM_IN), .REG_READ(and_23_out), .REG_WRITE(and_24_out), .C(C), .DATA_OUT(RAM_OUT),
    .INSIDE_REG_DATA(rejestr_4bit_11_inside_reg_data));

  // Other names for the same wires on the sheet: CLK = C; DATA_OUT[3:0] = RAM_OUT; READ = REG_READ; WRITE = REG_WRITE
endmodule

module ROM_REG (
  input  [31:0] DATA_IN,
  input  REG_WRITE,
  input  REG_READ,
  input  C,
  output [31:0] DATA_OUT
);

  wire [31:0] REG_A_q;

  Register #(.width(32)) REG_A (.D(DATA_IN), .en(REG_WRITE), .clk(C), .Q(REG_A_q));  // open: clr
  assign DATA_OUT = REG_READ ? REG_A_q : 32'bz;  // Controlled_Buffer controlled_buffer_1
endmodule

module MAKRO_TO_COPY (
  input  [3:0] REG_READ,
  input  [3:0] REG_WRITE,
  input  CARRY_IN,
  input  F1,
  input  F2,
  input  [1:0] STATE,
  input  [3:0] RAM_ADR,
  input  RAM_READ,
  input  RAM_WRITE,
  input  RAM_ENABLE,
  input  [3:0] DATA_1
);

  wire ALU, CLK, DATA, RAM;

  Decoder #(.select(2)) decoder_1 (.out0(DATA), .out1(ALU), .out2(RAM), .sel(STATE));  // open: out3, en
  Clock C (.out(CLK));

  // Other names for the same wires on the sheet: ADR[3:0] = RAM_ADR; CRY = CARRY_IN; EN = RAM_ENABLE; READ = RAM_READ;
  //   A = REG_READ[0]; B = REG_READ[1]; C = REG_READ[2]; D = REG_READ[3]; A_R = REG_WRITE[0]; B_R = REG_WRITE[1];
  //   C_R = REG_WRITE[2]; D_R = REG_WRITE[3]; WRITE = RAM_WRITE

  // Notes on the sheet:
  //   F1 F2
  //    0 0 ADD
  //   1 0 OR
  //   0 1 AND
  //   1 1 COMPARE
endmodule

module IO_MODULE (
  input  [3:0] I0_IN,
  input  REG_READ,
  input  REG_WRITE,
  input  ENABLE,
  input  [3:0] ADDRES,
  input  [3:0] PORT0_IN,
  input  C,
  output [3:0] IO_OUT,
  output [3:0] OUT_REG_13,
  output [3:0] OUT_REG_14
);

  wire and_1_out, and_2_out, and_3_out, and_4_out, and_5_out, and_6_out, and_7_out, and_8_out, REG_13,
       REG_14, REG_15, REG_16;
  wire [3:0] rejestr_4bit_1_inside_reg_data, rejestr_4bit_2_inside_reg_data, rejestr_4bit_3_inside_reg_data,
       rejestr_4bit_4_inside_reg_data;

  Decoder #(.select(4)) decoder_1 (
    .out12(REG_13), .out13(REG_14), .out14(REG_15), .out15(REG_16), .sel(ADDRES), .en(ENABLE));  // open: out0, out1, out2, out3, out4, out5, out6, out7, out8, out9, out10, out11
  Pull_Resistor pull_resistor_1 (.node(PORT0_IN));
  and and_1 (and_1_out, REG_READ, REG_13);
  and and_2 (and_2_out, REG_WRITE, REG_13);
  and and_3 (and_3_out, REG_READ, REG_14);
  and and_4 (and_4_out, REG_WRITE, REG_14);
  REJESTR_4BIT rejestr_4bit_1 (
    .DATA_IN(I0_IN), .REG_READ(and_1_out), .REG_WRITE(and_2_out), .C(C), .DATA_OUT(OUT_REG_13),
    .INSIDE_REG_DATA(rejestr_4bit_1_inside_reg_data));
  REJESTR_4BIT rejestr_4bit_2 (
    .DATA_IN(I0_IN), .REG_READ(and_3_out), .REG_WRITE(and_4_out), .C(C), .DATA_OUT(OUT_REG_14),
    .INSIDE_REG_DATA(rejestr_4bit_2_inside_reg_data));
  and and_5 (and_5_out, REG_READ, REG_15);
  and and_6 (and_6_out, REG_WRITE, REG_15);
  and and_7 (and_7_out, REG_READ, REG_16);
  and and_8 (and_8_out, REG_WRITE, REG_16);
  REJESTR_4BIT rejestr_4bit_3 (
    .DATA_IN(PORT0_IN), .REG_READ(and_5_out), .REG_WRITE(and_6_out), .C(C), .DATA_OUT(IO_OUT),
    .INSIDE_REG_DATA(rejestr_4bit_3_inside_reg_data));
  REJESTR_4BIT rejestr_4bit_4 (
    .DATA_IN(PORT0_IN), .REG_READ(and_7_out), .REG_WRITE(and_8_out), .C(C), .DATA_OUT(IO_OUT),
    .INSIDE_REG_DATA(rejestr_4bit_4_inside_reg_data));

  // Other names for the same wires on the sheet: CLK = C; DATA_OUT[3:0] = IO_OUT; READ = REG_READ; WRITE = REG_WRITE
endmodule

module ROM_MEMORY (
  input  [31:0] ROM_IN_PROGRAM,
  input  NEXT_CELL,
  input  C,
  input  START_PROGRAM,
  input  [3:0] SET_0000,
  input  PC_READ,
  input  PC_WRITE,
  input  [3:0] END_PROGRAM,
  input  [3:0] SET_0,
  input  [3:0] FLAGS,
  input  PROGRAM,
  input  [3:0] COUNTER_SET_0001,
  input  PROG_READ,
  input  PROG_WRITE,
  output [31:0] ROM_OUT,
  output [3:0] INSTRUCTION,
  output [3:0] PROG_COUNTER
);

  wire binary_to_bcd_converter_1_p2, binary_to_bcd_converter_1_p5, comparator_1_gt, comparator_2_gt, JUMP,
       PROG1, PROG2, PROG3, PROG4, PROG5, PROG6, PROG7, PROG8, PROG9, PROG10, PROG11, PROG12, PROG13, PROG14,
       PROG15, PROG16, REG_1, REG_2, REG_3, REG_4, REG_5, REG_6, REG_7, REG_8, REG_9, REG_10, REG_11, REG_12,
       REG_13, REG_14, REG_15, REG_16;
  wire [1:1] comparator_2_eq;
  wire [3:0] binary_to_bcd_converter_1_p1, multiplexer_1_out, pull_resistor_1_node, pull_resistor_2_node,
       rejestr_4bit_1_data_out;

  Comparator #(.width(4)) comparator_1 (.a(ROM_OUT[7:4]), .b(SET_0), .gt(comparator_1_gt));  // open: eq, lt
  Comparator #(.width(4)) comparator_2 (
    .a(ROM_OUT[3:0]), .b(END_PROGRAM), .gt(comparator_2_gt), .eq(comparator_2_eq[1]));  // open: lt
  and and_1 (JUMP, comparator_1_gt, FLAGS[0]);
  and and_2 (JUMP, comparator_1_gt, FLAGS[1]);
  Multiplexer #(.select(2), .width(4)) multiplexer_1 (
    .in0(binary_to_bcd_converter_1_p1), .in1(ROM_OUT[7:4]), .in3(SET_0000), .out(multiplexer_1_out),
    .sel({comparator_2_eq[1], JUMP}));  // open: in2
  Pull_Resistor pull_resistor_1 (.node(pull_resistor_1_node));
  Adder #(.width(4)) adder_1 (
    .a(multiplexer_1_out), .b(COUNTER_SET_0001), .out(pull_resistor_1_node));  // open: cin, cout
  _7_Segment_Display u_7_segment_display_1 ();  // open: g, f, a, b, e, d, c, dp
  // BCD_to_7_Segment_decoder bcd_to_7_segment_decoder_1: pin names not known; wires that end beside it: PC_READ
  // Binary_to_BCD_converter #(.binvalue(4)) binary_to_bcd_converter_1: pin names not known; wires that end beside it: binary_to_bcd_converter_1_p1, binary_to_bcd_converter_1_p2, binary_to_bcd_converter_1_p2, PROG_READ, binary_to_bcd_converter_1_p5
  Pull_Resistor pull_resistor_2 (.node(pull_resistor_2_node));
  Adder #(.width(4)) adder_2 (
    .a(rejestr_4bit_1_data_out), .b(COUNTER_SET_0001), .out(pull_resistor_2_node));  // open: cin, cout
  Pull_Resistor pull_resistor_3 (.node(ROM_OUT));
  REJESTR_4BIT PC_COUNTER (
    .DATA_IN(pull_resistor_1_node), .REG_READ(PC_READ), .REG_WRITE(PC_WRITE), .C(C),
    .DATA_OUT(binary_to_bcd_converter_1_p1), .INSIDE_REG_DATA(INSTRUCTION));
  _7_Segment_Display u_7_segment_display_2 ();  // open: g, f, a, b, e, d, c, dp
  // BCD_to_7_Segment_decoder bcd_to_7_segment_decoder_2: pin names not known; wires that end beside it: binary_to_bcd_converter_1_p5
  REJESTR_4BIT rejestr_4bit_1 (
    .DATA_IN(pull_resistor_2_node), .REG_READ(PROG_READ), .REG_WRITE(PROG_WRITE), .C(NEXT_CELL),
    .DATA_OUT(rejestr_4bit_1_data_out), .INSIDE_REG_DATA(PROG_COUNTER));
  Decoder #(.select(4)) decoder_1 (
    .out0(REG_1), .out1(REG_2), .out2(REG_3), .out3(REG_4), .out4(REG_5), .out5(REG_6), .out6(REG_7),
    .out7(REG_8), .out8(REG_9), .out9(REG_10), .out10(REG_11), .out11(REG_12), .out12(REG_13),
    .out13(REG_14), .out14(REG_15), .out15(REG_16), .sel(binary_to_bcd_converter_1_p1), .en(START_PROGRAM));
  Decoder #(.select(4)) decoder_2 (
    .out0(PROG1), .out1(PROG2), .out2(PROG3), .out3(PROG4), .out4(PROG5), .out5(PROG6), .out6(PROG7),
    .out7(PROG8), .out8(PROG9), .out9(PROG10), .out10(PROG11), .out11(PROG12), .out12(PROG13),
    .out13(PROG14), .out14(PROG15), .out15(PROG16), .sel(rejestr_4bit_1_data_out), .en(PROGRAM));
  ROM_REG rom_reg_1 (.DATA_IN(ROM_IN_PROGRAM), .REG_WRITE(PROG1), .REG_READ(REG_1), .C(C), .DATA_OUT(ROM_OUT));
  ROM_REG rom_reg_2 (.DATA_IN(ROM_IN_PROGRAM), .REG_WRITE(PROG2), .REG_READ(REG_2), .C(C), .DATA_OUT(ROM_OUT));
  ROM_REG rom_reg_3 (.DATA_IN(ROM_IN_PROGRAM), .REG_WRITE(PROG3), .REG_READ(REG_3), .C(C), .DATA_OUT(ROM_OUT));
  ROM_REG rom_reg_4 (.DATA_IN(ROM_IN_PROGRAM), .REG_WRITE(PROG4), .REG_READ(REG_4), .C(C), .DATA_OUT(ROM_OUT));
  ROM_REG rom_reg_5 (.DATA_IN(ROM_IN_PROGRAM), .REG_WRITE(PROG5), .REG_READ(REG_5), .C(C), .DATA_OUT(ROM_OUT));
  ROM_REG rom_reg_6 (.DATA_IN(ROM_IN_PROGRAM), .REG_WRITE(PROG6), .REG_READ(REG_6), .C(C), .DATA_OUT(ROM_OUT));
  ROM_REG rom_reg_7 (.DATA_IN(ROM_IN_PROGRAM), .REG_WRITE(PROG7), .REG_READ(REG_7), .C(C), .DATA_OUT(ROM_OUT));
  ROM_REG rom_reg_8 (.DATA_IN(ROM_IN_PROGRAM), .REG_WRITE(PROG8), .REG_READ(REG_8), .C(C), .DATA_OUT(ROM_OUT));
  ROM_REG rom_reg_9 (.DATA_IN(ROM_IN_PROGRAM), .REG_WRITE(PROG9), .REG_READ(REG_9), .C(C), .DATA_OUT(ROM_OUT));
  ROM_REG rom_reg_10 (.DATA_IN(ROM_IN_PROGRAM), .REG_WRITE(PROG10), .REG_READ(REG_10), .C(C), .DATA_OUT(ROM_OUT));
  ROM_REG rom_reg_11 (.DATA_IN(ROM_IN_PROGRAM), .REG_WRITE(PROG11), .REG_READ(REG_11), .C(C), .DATA_OUT(ROM_OUT));
  ROM_REG rom_reg_12 (.DATA_IN(ROM_IN_PROGRAM), .REG_WRITE(PROG12), .REG_READ(REG_12), .C(C), .DATA_OUT(ROM_OUT));
  ROM_REG rom_reg_13 (.DATA_IN(ROM_IN_PROGRAM), .REG_WRITE(PROG13), .REG_READ(REG_13), .C(C), .DATA_OUT(ROM_OUT));
  ROM_REG rom_reg_14 (.DATA_IN(ROM_IN_PROGRAM), .REG_WRITE(PROG14), .REG_READ(REG_14), .C(C), .DATA_OUT(ROM_OUT));
  ROM_REG rom_reg_15 (.DATA_IN(ROM_IN_PROGRAM), .REG_WRITE(REG_15), .REG_READ(REG_15), .C(C), .DATA_OUT(ROM_OUT));
  ROM_REG rom_reg_16 (.DATA_IN(ROM_IN_PROGRAM), .REG_WRITE(REG_16), .REG_READ(REG_16), .C(C), .DATA_OUT(ROM_OUT));

  // Other names for the same wires on the sheet: CLK = C; counter[3:0] = COUNTER_SET_0001; DATA_OUT[31:0] = ROM_OUT;
  //   LAST_4[3:0] = ROM_OUT[3:0]; PENULTIMATE_4[3:0] = ROM_OUT[7:4]; PROGRAM_NEXTBLOCK = NEXT_CELL
endmodule
